# Fritzing sketch AmpMonitor (saved by Fritzing 0.9.3b)

parts:
  U1 = ESP32S-HiLetgo [part_number=ESP32S-HiLetgo]
  Part1 = Adafruit ADS1115 16Bit I2C ADC [part_number="Adafruit #1085"]
  JP1 = USB_MICROB_PLUG [package=micro-b-ra-smt]
  TFT_128x1 = TFT 128x160 [package="SIP (Single Inline) [THT]"]
  M1 = RioRand LM2596
  U2 = TMP36 [package=to-92]
  Power_plug1 = Power plug

nets:
  GND: U1.GND, Part1.ADDR, Part1.GND, TFT_128x1.LED-, M1.Pin_4, U2.GND
  VIN: U1.VIN, Part1.VDD, TFT_128x1.LED+, M1.Pin_3, U2.VCC
  N1: U1.GPIO2, TFT_128x1.A0
  N2: U1.GPIO4, TFT_128x1.RESET
  N3: U1.GPIO5, TFT_128x1.CS
  N4: U1.GPIO18, TFT_128x1.SCL
  N5: U1.GPIO21, Part1.SDA
  N6: U1.GPIO22, Part1.SCL
  N7: U1.GPIO23, TFT_128x1.SDA
  N8: Part1.AIN3, U2.VOUT
  N9: Part1.AIN1, Power_plug1.VCC
  N10: Part1.AIN0, Power_plug1.GND
  N11: JP1.VCC, M1.Pin_1
  N12: JP1.GND, M1.Pin_2

notes:
  Amp Bias
  Temperature Sensor

custom parts:
  ESP32S-HiLetgo: HiLetgo ESP-WROOM-32 ESP32 ESP-32S Development Board 2.4GHz Dual-Mode WiFi + Bluetooth Dual Cores Microcontroller The ESP32 integrated with Antenna switches, RF Balun, power amplifiers, low-noise amplifiers, filters, and management modules, and the entire solution occupies the least area of PCB. 2.4 GHz Wi-Fi plus Bluetooth dual-mode chip, with TSMC Ultra-low power consumption 40nm technology,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
  Adafruit ADS1115 16Bit I2C ADC: For microcontrollers without an analog-to-digital converter or when you want a higher-precision ADC, the ADS1115 provides 16-bit precision at 860 samples/second over I2C. The chip can be configured as 4 single-ended input channels, or two differential channels. As a nice bonus, it even includes a programmable gain amplifier, up to x16, to help boost up smaller single/differential signals to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
